# Fritzing sketch nfc_project (saved by Fritzing 1.0.1rc)
breadboards: 1

parts:
  Mod1 = Raspberry Pi 4B
  Деталь1 = PN532 Elechouse RFID NFC Module V3
  IC1 = 2.8 inch LCD SPI display with touch screen & SD card

nets:
  5V: Mod1.5V, Деталь1.VCC, IC1.pin1
  GND: Mod1.GND, Деталь1.GND, IC1.pin2
  N1: Mod1.GPIO4, Деталь1.SS
  N2: Mod1.GPIO18, IC1.pin3
  N3: Mod1.GPIO27, Деталь1.RSTO
  N4: Mod1.GPIO23, IC1.pin4
  N5: Mod1.GPIO24, IC1.pin5
  N6: Mod1.GPIO10, Деталь1.MOSI
  N7: Mod1.GPIO9, Деталь1.MISO
  N8: Mod1.GPIO25, IC1.pin8
  N9: Mod1.GPIO11, Деталь1.SCK
  N10: Mod1.GPIO19, IC1.pin_9
  N11: Mod1.GPIO20, IC1.pin6
  N12: Mod1.GPIO21, IC1.pin7

custom parts:
  PN532 Elechouse RFID NFC Module V3: NFC is a popular technology in recent years. We often heard this work while smart phone company such as Samsung or HTC introduces their latest high-end phones. Almost all the high-end phone in the market support NFC. Near field communication (NFC) is a set of standards for smart phones and similar devices to establish radio communication with each other by touching them together or bringing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
  2.8 inch LCD SPI display with touch screen & SD card: A generic 2.8 inch LCD TFT 320x280 display with touchscreen and SD card slot.
